// Logisim project hw4part1.circ as structural Verilog: 2 circuits, main circuit Register
module Tester (
  input  [7:0] Input,
  input  Enable,
  output [7:0] Output
);

  wire Clock_out, Reset_out;

  Register register_1 (.Data_In(Input), .Data_Out(Output), .Clock(Clock_out), .Reset(Reset_out), .Enable(Enable));
  Clock Clock (.out(Clock_out));
  Button Reset (.out(Reset_out));

  // Notes on the sheet:
  //   You can use this to test your circuit.
endmodule

module Register (
  input  [7:0] Data_In,
  input  Clock,
  input  Reset,
  input  Enable,
  output [7:0] Data_Out
);


  // Other names for the same wires on the sheet: CLK = Clock; D[7:0] = Data_In; EN = Enable; Q[7:0] = Data_Out;
  //   RST = Reset

  // Notes on the sheet:
  //   Implement your register circuit here!
  //   My name is
  //   [your name here]
  //   and this is my pretty 8-bit register!
endmodule
