// Logisim project hw4part2.circ as structural Verilog: 2 circuits, main circuit One-Hot State Machine
module Tester (
  input  G
);

  wire Clock_out, one_hot_state_machine_1_w, one_hot_state_machine_1_x, one_hot_state_machine_1_y,
       one_hot_state_machine_1_z, Reset_out;

  One_Hot_State_Machine one_hot_state_machine_1 (
    .W(one_hot_state_machine_1_w), .Clock(Clock_out), .Reset(Reset_out), .G(G),
    .X(one_hot_state_machine_1_x), .Y(one_hot_state_machine_1_y), .Z(one_hot_state_machine_1_z));
  Clock Clock (.out(Clock_out));
  LED W (.in(one_hot_state_machine_1_w));
  LED X (.in(one_hot_state_machine_1_x));
  LED Y (.in(one_hot_state_machine_1_y));
  LED Z (.in(one_hot_state_machine_1_z));
  Button Reset (.out(Reset_out));

  // Notes on the sheet:
  //   You can use this to test your circuit.
endmodule

module One_Hot_State_Machine (
  input  G,
  input  Clock,
  input  Reset,
  output W,
  output X,
  output Y,
  output Z
);

  wire and_4_out, and_5_out, and_6_out, and_8_out, and_9_out, and_10_out, and_11_out, and_12_out, and_13_out,
       and_14_out, D0, D1, D2, D3, D4, D5, D6, nG, nor_1_out, not_1_out, Q0, Q1, Q2, Q3, Q4, Q5, Q6;
  wire [0:0] or_4_out;

  and and_1 (D0, nG, Q6);
  and and_2 (D1, G, Q0);
  and and_3 (D2, nG, Q1);
  and and_4 (and_4_out, nG, Q2);
  and and_5 (and_5_out, nG, Q3);
  and and_6 (and_6_out, G, Q2);
  and and_7 (D4, G, Q1);
  and and_8 (and_8_out, nG, Q4);
  and and_9 (and_9_out, G, Q3);
  and and_10 (and_10_out, G, Q4);
  and and_11 (and_11_out, nG, Q5);
  and and_12 (and_12_out, G, Q5);
  and and_13 (and_13_out, G, Q6);
  or or_1 (D3, and_4_out, and_5_out, and_6_out);
  or or_2 (D5, and_8_out, and_9_out, and_10_out);
  or or_3 (D6, and_11_out, and_12_out, and_13_out);
  nor nor_1 (nor_1_out, G, Clock);
  and and_14 (and_14_out, nor_1_out, not_1_out);
  not not_1 (not_1_out, D0);
  or or_4 (or_4_out[0], and_14_out, D0);
  not not_2 (nG, G);
  Register #(.width(7)) register_1 (
    .D({D6, D5, D4, D3, D2, D1, or_4_out[0]}), .Q({Q6, Q5, Q4, Q3, Q2, Q1, Q0}), .clk(Clock), .clr(Reset));  // open: en
  or or_5 (W, Q2, Q3, Q6);
  or or_6 (X, Q0, Q3);
  or or_7 (Y, Q3, Q5, Q6);
  or or_8 (Z, Q2, Q4, Q5);

  // Other names for the same wires on the sheet: CLK = Clock; RST = Reset

  // Notes on the sheet:
  //   My name is
  //   Jesse Chen
  //   and this is my pretty one-hot state machine!
endmodule
